# Fritzing sketch quadcopterino_mk_I_cp (saved by Fritzing 0.8.3b)
circuit board: 5.5cm x 4.4cm
stripboards: 6
perfboards: 1

parts:
  Arduino1 = Arduino Mini (Rev5)
  M1 = DC Motor
  M2 = DC Motor
  M3 = DC Motor
  M4 = DC Motor
  IMU1 = MPU-9150 Breakout [package=THT]
  MiniFetOut = female pin header, 10 pins [form="♀ (female)"]
  +/- = female pin header, 2 pins [form="♀ (female)"]
  TTL = female pin header, 4 pins [form="♀ (female)"]
  IrSensor = IS471F [package=THT]
  J2 = female pin header, 2 pins [form="♀ (female)"]
  RX_TX = female pin header, 2 pins [form="♀ (female)"]
  IrLed = LED - 3mm [color="Red (633nm)" package="3 mm [THT]"]
  C1 = Electrolytic Capacitor [capacitance=0.1mF package="100 mil [THT, electrolytic]"]
  LiPwr_Vcc = female pin header, 2 pins [form="♀ (female)"]
  LiPwrBatt = double row female pin header, 2 pins [form="♀ (female)"]
  PwrSel = female pin header, 3 pins [form="♀ (female)"]
  C2 = SuperCap 25F 2.5V [package="200 mil [THT, electrolytic]"]
  C3 = SuperCap 25F 2.5V [package="200 mil [THT, electrolytic]"]
  C4 = SuperCap 25F 2.5V [package="200 mil [THT, electrolytic]"]
  C5 = SuperCap 25F 2.5V [package="200 mil [THT, electrolytic]"]
  J4 = female pin header, 2 pins [form="♀ (female)"]  # not connected
  C6 = Ceramic Capacitor [capacitance=100nF package="100 mil [THT, multilayer]"]
  C7 = Ceramic Capacitor [capacitance=100nF package="100 mil [THT, multilayer]"]
  C8 = Ceramic Capacitor [capacitance=100nF package="100 mil [THT, multilayer]"]
  C9 = Ceramic Capacitor [capacitance=100nF package="100 mil [THT, multilayer]"]
  C10 = Ceramic Capacitor [capacitance=100nF package="200 mil [THT, multilayer]"]
  C11 = Ceramic Capacitor [capacitance=100nF package="200 mil [THT, multilayer]"]
  C12 = Ceramic Capacitor [capacitance=100nF package="100 mil [THT, multilayer]"]
  C13 = Ceramic Capacitor [capacitance=100nF package="100 mil [THT, multilayer]"]
  C14 = Ceramic Capacitor [capacitance=100nF package="100 mil [THT, multilayer]"]
  C15 = Ceramic Capacitor [capacitance=100nF package="100 mil [THT, multilayer]"]
  C16 = Ceramic Capacitor [capacitance=100nF package="100 mil [THT, multilayer]"]
  C17 = Ceramic Capacitor [capacitance=100nF package="100 mil [THT, multilayer]"]
  C18 = Electrolytic Capacitor [capacitance=1µF package="300 mil [THT, electrolytic]"]
  C19 = Electrolytic Capacitor [capacitance=1µF package="300 mil [THT, electrolytic]"]
  C20 = Electrolytic Capacitor [capacitance=1µF package="300 mil [THT, electrolytic]"]
  C21 = Electrolytic Capacitor [capacitance=1µF package="300 mil [THT, electrolytic]"]
  LiPwrBatt1 = double row female pin header, 2 pins [form="♀ (female)"]
  +/-_2 = female pin header, 2 pins [form="♀ (female)"]
  Vcc = female pin header, 2 pins [form="♀ (female)"]

nets:
  N1: Arduino1.D2, IMU1.INT
  N2: Arduino1.A4, IMU1.SCL
  N3: Arduino1.A5, IMU1.SDA
  5V: Arduino1.5V, IMU1.Vcc
  5V_2: M1.pin_1, M2.pin_2, M3.pin_2, M4.pin_1, TTL.pin3, IrSensor.vcc, IrLed.anode, C1.+, C8.1, C11.0, C12.1, C13.0, C14.1, C15.1, C16.1, Vcc.pin1
  N4: M1.pin_2, MiniFetOut.pin7, C16.0, C17.0
  N5: M2.pin_1, MiniFetOut.pin1, C10.1, C14.0
  N6: M3.pin_1, MiniFetOut.pin3, C9.0, C13.1
  N7: M4.pin_2, MiniFetOut.pin4, C7.0, C12.0
  GND: +/-.pin1, TTL.pin4, IrSensor.GND, C1.-, LiPwr_Vcc.pin2, LiPwrBatt.pin2, C4.-, C5.-, C6.0, C7.1, C8.0, C9.1, C10.0, C11.1, C15.0, C17.1, C19.-, C20.-, LiPwrBatt1.pin2, +/-_2.pin1
  N8: +/-.pin2, PwrSel.pin1, C3.+, C21.+, +/-_2.pin2
  N9: TTL.pin1, RX_TX.pin1
  N10: TTL.pin2, RX_TX.pin2
  N11: IrSensor.Vo, J2.pin1
  N12: IrSensor.GDout, IrLed.cathode
  N13: LiPwrBatt.pin1, PwrSel.pin3, LiPwrBatt1.pin1
  N14: PwrSel.pin2, C2.+, C18.+
  N15: C2.-, C4.+, C18.-, C20.+
  N16: C3.-, C5.+, C19.+, C21.-

notes:
  A
  B
  Mk. I
  Attribution Share-Alike 3.0 License
  Released under the Creative Commons
  is nothing more to add, but
  is attained, not when there
  Not approved
  MiniFET metashield
  (c) 2013 <luis@ontanon.org>
  for manned flight.
  quadricopterino
  -- Antoine Saint Euxpery
  when there is nothing
  more to take away.
  It seems that perfection
  tx  rx  vcc gnd
  Quadcopterino Mk. I : The PoC. Implemented as a sandwich using an IMU (not connected here) on top of an Arduino Mini on top sparkfun's Arduino-mini's Mini FET shield, on top of THIS shield that provides for a 2x2 array of SuperCaps and connections (motors, TTL) on top of a LiPower Shield as secondary power
  LiPower
  IMU
  TTL
  Hacks needed:
  - UVLO has to be zeroed in LiPower (shorting R3)
  - Current to the FETs has to change to 5V in the MiniFET
  Rev History:
  Rel1a:
  - added supercaps and connectos
  Rel1a->Rel1b:
  - added a TTL breakout
  - change jumpers for large vias, (It still can be printed on one layer only and routed with just four wires)
  Rel1b->Rel1c:
  - Added a jumper to select whether the 2nd series of capacitors (A2, B2) pass thru an external LiPwr or are just put in paralel with A1 and B.
  -Added a second battery plug
  - Added capacitors to shield from motor noise
  - Added logos and other deco
  - Added an aircraft pioneer's quotation to keep in mind... this is an aircraft part, it has to be as light as possible .
  Proximity Sensor
  http://www.quadricopterino.org

custom parts:
  MPU-9150 Breakout: Generic female header
  IS471F: SHARP's IS471F Ir detector
  SuperCap 25F 2.5V: 25F 2.5V Super Capacitor
